# Fritzing sketch circuit_diagram (saved by Fritzing 0.9.4)
breadboards: 1

parts:
  Raspberry_Pi_1 = Raspberry Pi 3 [part_number=RPI-3-V1.2]
  LED1 = LED - 5mm [color="Red (633nm)" package="5 mm [THT]"]
  R1 = Resistor [tolerance=±5% resistance=560 package=THT]
  R2 = Resistor [tolerance=±5% resistance=560 package=THT]
  LED2 = LED - 5mm [color="Green (570nm)" package="5 mm [THT]"]
  Part1 = Arduino Uno (Rev3)
  Q1 = NPN-Transistor [package="TO92 [THT]"]
  Q2 = NPN-Transistor [package="TO92 [THT]"]
  Q3 = NPN-Transistor [package="TO92 [THT]"]
  R3 = Resistor [tolerance=±5% resistance=1M package=THT]
  R4 = Resistor [tolerance=±5% resistance=1M package=THT]
  R5 = Resistor [tolerance=±5% resistance=1M package=THT]
  Q4 = NPN-Transistor [package="TO92 [THT]"]
  R6 = Resistor [tolerance=±5% resistance=1M package=THT]
  S1 = Pushbutton [package="[THT]"]
  S2 = Pushbutton [package="[THT]"]

nets:
  N1: Raspberry_Pi_1.GND, Q2.C, Q3.C, Q4.C
  N2: Raspberry_Pi_1.GPIO17, Q3.E
  N3: Raspberry_Pi_1.GPIO27, Q2.E
  N4: Raspberry_Pi_1.GPIO26, LED2.anode, Part1.D2
  N5: Raspberry_Pi_1.GPIO21, LED1.anode, Part1.D3_PWM
  N6: Raspberry_Pi_1.GPIO23, Q4.E
  N7: Raspberry_Pi_1.GPIO18, Q1.E
  N8: LED1.cathode, R1.Pin_0
  N9: R1.Pin_1, R2.Pin_1
  N10: R2.Pin_0, LED2.cathode
  N11: Part1.D8, R6.Pin_0
  N12: Part1.D9_PWM, R4.Pin_0
  N13: Part1.D10_PWM/SS, R5.Pin_0
  N14: Part1.D11_PWM/MOSI, R3.Pin_0
  N15: Part1.D4, S2.Pin_3, S2.Pin_4
  N16: Part1.D5_PWM, S1.Pin_3, S1.Pin_4
  N17: Q1.B, R3.Pin_1
  N18: Q2.B, R4.Pin_1
  N19: Q3.B, R5.Pin_1
  N20: Q4.B, R6.Pin_1
  N21: S1.Pin_1, S1.Pin_2
  N22: S2.Pin_1, S2.Pin_2
